# Fritzing sketch DIAGRAMAScircuitoEELETRO (saved by Fritzing 0.9.4)
breadboards: 1

parts:
  Componente1 = Arduino Uno (Rev3)
  DHT1 = Humidity and Temperature Sensor DHT11
  J1 = Basic Servo

nets:
  N1: Componente1.D5_PWM, DHT1.Data-signal
  N2: Componente1.D6_PWM, J1.pulse
  5V: Componente1.5V, J1.vcc
  GND: Componente1.GND, DHT1.GND_2, J1.gnd

custom parts:
  Humidity and Temperature Sensor DHT11: Digital relative humidity & temperature sensor DHT11

// code stored in the sketch: codigo.ino
#include "DHT.h"
#include <Servo.h>

#define DHTPIN 5

#define DHTTYPE DHT11

DHT dht(DHTPIN, DHTTYPE);
Servo servo;
float pos = 0;

void setup()
{
  Serial.begin(9600);
  servo.attach(6);

  dht.begin();
}

void loop()
{
  delay(2000);

  float h = dht.readHumidity();

  float t = dht.readTemperature();

  float f = dht.readTemperature(true);

  float hif = dht.computeHeatIndex(f, h);

  float hic = dht.computeHeatIndex(t, h, false);

  pos = t * 3.6;
  servo.write(pos);

  Serial.println(h);
}
